# Fritzing sketch head_fan (saved by Fritzing 0.9.2b)
breadboards: 1

parts:
  Q1 = NPN-Transistor [package="TO92 [THT]"]
  R1 = Resistor [tolerance=±5% resistance=330 package=THT]
  R2 = Resistor [tolerance=±5% resistance=1k package=THT]
  D1 = Rectifier Diode [part_number=1N4001 package="300 mil [THT]"]
  M1 = DC Motor

nets:
  GND: Q1.E, R2.Pin_1
  N1: Q1.B, R1.Pin_1, R2.Pin_0
  N2: Q1.C, D1.anode, M1.pin_2
  control: R1.Pin_0
  5V: D1.cathode, M1.pin_1
